// Digital circuit ALU 4bit.dig as structural Verilog
module ALU_4bit (
  input  S2,
  input  S1,
  input  S0,
  input  A_0,
  input  B_0,
  input  A_1,
  input  B_1,
  input  A_2,
  input  B_2,
  input  A_3,
  input  B_3,
  output Output_0,
  output Output_1,
  output Output_2,
  output Output_3,
  output Output_4
);

  wire and_1_out, and_2_out, and_3_out, and_4_out, and_5_out, and_6_out, and_7_out, and_8_out, and_9_out,
       and_10_out, and_11_out, and_12_out, and_13_out, and_14_out, and_15_out, and_16_out, and_17_out,
       and_18_out, and_19_out, and_20_out, and_21_out, and_22_out, and_23_out, and_24_out, and_25_out,
       and_26_out, and_27_out, and_28_out, and_29_out, and_30_out, and_31_out, and_32_out, and_33_out,
       and_34_out, and_35_out, and_36_out, and_37_out, and_38_out, and_39_out, and_40_out, and_41_out,
       and_42_out, and_43_out, and_44_out, and_45_out, and_46_out, and_47_out, and_48_out, and_49_out,
       and_50_out, and_51_out, and_52_out, and_53_out, and_54_out, and_55_out, and_56_out, and_57_out,
       and_58_out, and_59_out, and_60_out, and_61_out, and_62_out, and_63_out, and_64_out, and_65_out,
       and_66_out, and_67_out, and_68_out, and_69_out, and_70_out, and_71_out, and_72_out, and_73_out,
       and_74_out, and_75_out, and_76_out, and_77_out, and_78_out, and_79_out, and_80_out, and_81_out,
       and_82_out, and_83_out, and_84_out, and_85_out, and_86_out, and_87_out, and_88_out, and_89_out,
       and_90_out, and_91_out, and_92_out, and_93_out, and_94_out, and_95_out, and_96_out, and_97_out,
       and_98_out, and_99_out, and_100_out, and_101_out, and_102_out, nand_1_out, nand_2_out, nand_3_out,
       nand_4_out, not_1_out, not_2_out, not_3_out, not_4_out, not_5_out, not_6_out, not_7_out, not_8_out,
       not_9_out, not_10_out, not_11_out, not_12_out, not_13_out, not_14_out, not_15_out, not_16_out,
       not_17_out, not_18_out, not_19_out, not_20_out, not_21_out, not_22_out, not_23_out, not_24_out,
       not_25_out, not_26_out, not_27_out, not_28_out, not_29_out, not_30_out, not_31_out, not_32_out,
       not_33_out, not_34_out, not_35_out, not_36_out, not_37_out, not_38_out, not_39_out, not_40_out,
       not_41_out, not_42_out, not_43_out, not_44_out, not_45_out, not_46_out, not_47_out, not_48_out,
       not_49_out, not_50_out, not_51_out, not_52_out, not_53_out, not_54_out, not_55_out, or_1_out,
       or_2_out, or_3_out, or_4_out, or_5_out, or_6_out, or_7_out, or_8_out, or_9_out, or_10_out, or_11_out,
       or_12_out, or_13_out, or_14_out, or_15_out, or_16_out, or_17_out, or_18_out, or_19_out, or_20_out,
       or_26_out, or_27_out, or_28_out, or_29_out, or_30_out, or_31_out, or_32_out, or_33_out, or_34_out,
       or_35_out, or_36_out, or_37_out, or_38_out, xor_1_out, xor_2_out, xor_3_out, xor_4_out, xor_5_out,
       xor_6_out, xor_7_out, xor_8_out, xor_9_out, xor_10_out, xor_11_out, xor_12_out;

  not not_1 (not_1_out, S0);
  not not_2 (not_2_out, S0);
  not not_3 (not_3_out, S0);
  not not_4 (not_4_out, S0);
  not not_5 (not_5_out, S0);
  not not_6 (not_6_out, S0);
  not not_7 (not_7_out, S0);
  not not_8 (not_8_out, S0);
  not not_9 (not_9_out, S1);
  not not_10 (not_10_out, S1);
  not not_11 (not_11_out, S1);
  not not_12 (not_12_out, S1);
  not not_13 (not_13_out, S1);
  not not_14 (not_14_out, S1);
  not not_15 (not_15_out, S1);
  not not_16 (not_16_out, S1);
  not not_17 (not_17_out, A_0);
  not not_18 (not_18_out, B_0);
  not not_19 (not_19_out, A_1);
  not not_20 (not_20_out, B_1);
  not not_21 (not_21_out, A_2);
  not not_22 (not_22_out, B_2);
  not not_23 (not_23_out, A_3);
  not not_24 (not_24_out, B_3);
  and and_1 (and_1_out, A_0, not_9_out, not_1_out);
  and and_2 (and_2_out, not_17_out, not_9_out, S0);
  and and_3 (and_3_out, A_0, not_1_out, S1);
  and and_4 (and_4_out, A_0, S0, S1);
  and and_5 (and_5_out, not_18_out, not_10_out, not_2_out);
  and and_6 (and_6_out, B_0, not_10_out, S0);
  and and_7 (and_7_out, B_0, not_2_out, S1);
  and and_8 (and_8_out, 1'b0, S0, S1);
  and and_9 (and_9_out, A_1, not_11_out, not_3_out);
  and and_10 (and_10_out, not_19_out, not_11_out, S0);
  and and_11 (and_11_out, A_1, not_3_out, S1);
  and and_12 (and_12_out, A_1, S0, S1);
  and and_13 (and_13_out, not_20_out, not_12_out, not_4_out);
  and and_14 (and_14_out, B_1, not_12_out, S0);
  and and_15 (and_15_out, B_1, not_4_out, S1);
  and and_16 (and_16_out, 1'b0, S0, S1);
  and and_17 (and_17_out, A_2, not_13_out, not_5_out);
  and and_18 (and_18_out, not_21_out, not_13_out, S0);
  and and_19 (and_19_out, A_2, not_5_out, S1);
  and and_20 (and_20_out, A_2, S0, S1);
  and and_21 (and_21_out, not_22_out, not_14_out, not_6_out);
  and and_22 (and_22_out, B_2, not_14_out, S0);
  and and_23 (and_23_out, B_2, not_6_out, S1);
  and and_24 (and_24_out, 1'b0, S0, S1);
  and and_25 (and_25_out, A_3, not_15_out, not_7_out);
  and and_26 (and_26_out, not_23_out, not_15_out, S0);
  and and_27 (and_27_out, A_3, not_7_out, S1);
  and and_28 (and_28_out, A_3, S0, S1);
  and and_29 (and_29_out, not_24_out, not_16_out, not_8_out);
  and and_30 (and_30_out, B_3, not_16_out, S0);
  and and_31 (and_31_out, B_3, not_8_out, S1);
  and and_32 (and_32_out, 1'b0, S0, S1);
  or or_1 (or_1_out, and_1_out, and_2_out, and_3_out, and_4_out);
  or or_2 (or_2_out, and_5_out, and_6_out, and_7_out, and_8_out);
  or or_3 (or_3_out, and_9_out, and_10_out, and_11_out, and_12_out);
  or or_4 (or_4_out, and_13_out, and_14_out, and_15_out, and_16_out);
  or or_5 (or_5_out, and_17_out, and_18_out, and_19_out, and_20_out);
  or or_6 (or_6_out, and_21_out, and_22_out, and_23_out, and_24_out);
  or or_7 (or_7_out, and_25_out, and_26_out, and_27_out, and_28_out);
  or or_8 (or_8_out, and_29_out, and_30_out, and_31_out, and_32_out);
  or or_9 (or_9_out, or_1_out, or_2_out);
  xor xor_1 (xor_1_out, or_1_out, or_2_out);
  nand nand_1 (nand_1_out, or_1_out, or_2_out);
  or or_10 (or_10_out, or_1_out, or_2_out);
  or or_11 (or_11_out, or_3_out, or_4_out);
  xor xor_2 (xor_2_out, or_3_out, or_4_out);
  nand nand_2 (nand_2_out, or_3_out, or_4_out);
  or or_12 (or_12_out, or_3_out, or_4_out);
  or or_13 (or_13_out, or_5_out, or_6_out);
  xor xor_3 (xor_3_out, or_5_out, or_6_out);
  nand nand_3 (nand_3_out, or_5_out, or_6_out);
  or or_14 (or_14_out, or_5_out, or_6_out);
  or or_15 (or_15_out, or_7_out, or_8_out);
  xor xor_4 (xor_4_out, or_7_out, or_8_out);
  nand nand_4 (nand_4_out, or_7_out, or_8_out);
  or or_16 (or_16_out, or_7_out, or_8_out);
  not not_25 (not_25_out, S0);
  not not_26 (not_26_out, S0);
  not not_27 (not_27_out, S0);
  not not_28 (not_28_out, S0);
  not not_29 (not_29_out, S1);
  not not_30 (not_30_out, S1);
  not not_31 (not_31_out, S1);
  not not_32 (not_32_out, S1);
  and and_33 (and_33_out, or_9_out, not_29_out, not_25_out);
  and and_34 (and_34_out, xor_1_out, not_29_out, S0);
  and and_35 (and_35_out, nand_1_out, not_25_out, S1);
  and and_36 (and_36_out, or_10_out, S0, S1);
  and and_37 (and_37_out, or_11_out, not_30_out, not_26_out);
  and and_38 (and_38_out, xor_2_out, not_30_out, S0);
  and and_39 (and_39_out, nand_2_out, not_26_out, S1);
  and and_40 (and_40_out, or_12_out, S0, S1);
  and and_41 (and_41_out, or_13_out, not_31_out, not_27_out);
  and and_42 (and_42_out, xor_3_out, not_31_out, S0);
  and and_43 (and_43_out, nand_3_out, not_27_out, S1);
  and and_44 (and_44_out, or_14_out, S0, S1);
  and and_45 (and_45_out, or_15_out, not_32_out, not_28_out);
  and and_46 (and_46_out, xor_4_out, not_32_out, S0);
  and and_47 (and_47_out, nand_4_out, not_28_out, S1);
  and and_48 (and_48_out, or_16_out, S0, S1);
  or or_17 (or_17_out, and_33_out, and_34_out, and_35_out, and_36_out);
  or or_18 (or_18_out, and_37_out, and_38_out, and_39_out, and_40_out);
  or or_19 (or_19_out, and_41_out, and_42_out, and_43_out, and_44_out);
  or or_20 (or_20_out, and_45_out, and_46_out, and_47_out, and_48_out);
  not not_33 (not_33_out, S2);
  and and_49 (and_49_out, S2, or_17_out);
  or or_21 (Output_0, and_50_out, and_49_out);
  and and_50 (and_50_out, xor_11_out, not_33_out);
  and and_51 (and_51_out, S2, or_18_out);
  and and_52 (and_52_out, not_33_out, xor_12_out);
  or or_22 (Output_1, and_52_out, and_51_out);
  and and_53 (and_53_out, S2, or_19_out);
  or or_23 (Output_2, and_54_out, and_53_out);
  and and_54 (and_54_out, not_33_out, xor_9_out);
  and and_55 (and_55_out, S2, or_20_out);
  and and_56 (and_56_out, not_33_out, xor_10_out);
  or or_24 (Output_3, and_56_out, and_55_out);
  and and_57 (and_57_out, S2, 1'b0);
  or or_25 (Output_4, and_58_out, and_57_out);
  and and_58 (and_58_out, not_33_out, or_36_out);
  not not_34 (not_34_out, S0);
  not not_35 (not_35_out, S0);
  not not_36 (not_36_out, S0);
  not not_37 (not_37_out, S0);
  not not_38 (not_38_out, S0);
  not not_39 (not_39_out, S0);
  not not_40 (not_40_out, S0);
  not not_41 (not_41_out, S0);
  not not_42 (not_42_out, S1);
  not not_43 (not_43_out, S1);
  not not_44 (not_44_out, S1);
  not not_45 (not_45_out, S1);
  not not_46 (not_46_out, S1);
  not not_47 (not_47_out, S1);
  not not_48 (not_48_out, S1);
  not not_49 (not_49_out, S1);
  not not_50 (not_50_out, A_3);
  not not_51 (not_51_out, A_2);
  and and_59 (and_59_out, A_3, not_44_out, not_34_out);
  and and_60 (and_60_out, B_3, not_44_out, S0);
  and and_61 (and_61_out, not_50_out, not_34_out, S1);
  and and_62 (and_62_out, A_3, S0, S1);
  and and_63 (and_63_out, B_3, not_45_out, not_35_out);
  and and_64 (and_64_out, B_3, not_45_out, S0);
  and and_65 (and_65_out, B_3, not_35_out, S1);
  and and_66 (and_66_out, 1'b0, S0, S1);
  not not_52 (not_52_out, A_0);
  not not_53 (not_53_out, A_1);
  and and_67 (and_67_out, A_2, not_42_out, not_38_out);
  and and_68 (and_68_out, B_2, not_42_out, S0);
  and and_69 (and_69_out, not_51_out, not_38_out, S1);
  and and_70 (and_70_out, A_2, S0, S1);
  and and_71 (and_71_out, B_2, not_43_out, not_39_out);
  and and_72 (and_72_out, B_2, not_43_out, S0);
  and and_73 (and_73_out, B_2, not_39_out, S1);
  and and_74 (and_74_out, 1'b0, S0, S1);
  and and_75 (and_75_out, A_0, not_46_out, not_40_out);
  and and_76 (and_76_out, B_0, not_46_out, S0);
  and and_77 (and_77_out, not_52_out, not_40_out, S1);
  and and_78 (and_78_out, A_0, S0, S1);
  and and_79 (and_79_out, B_0, not_47_out, not_41_out);
  and and_80 (and_80_out, B_0, not_47_out, S0);
  and and_81 (and_81_out, B_0, not_41_out, S1);
  and and_82 (and_82_out, 1'b0, S0, S1);
  and and_83 (and_83_out, A_1, not_48_out, not_36_out);
  and and_84 (and_84_out, B_1, not_48_out, S0);
  and and_85 (and_85_out, not_53_out, not_36_out, S1);
  and and_86 (and_86_out, A_1, S0, S1);
  and and_87 (and_87_out, B_1, not_49_out, not_37_out);
  and and_88 (and_88_out, B_1, not_49_out, S0);
  and and_89 (and_89_out, B_1, not_37_out, S1);
  and and_90 (and_90_out, 1'b0, S0, S1);
  or or_26 (or_26_out, and_59_out, and_60_out, and_61_out, and_62_out);
  or or_27 (or_27_out, and_63_out, and_64_out, and_65_out, and_66_out);
  or or_28 (or_28_out, and_83_out, and_84_out, and_85_out, and_86_out);
  or or_29 (or_29_out, and_87_out, and_88_out, and_89_out, and_90_out);
  or or_30 (or_30_out, and_67_out, and_68_out, and_69_out, and_70_out);
  or or_31 (or_31_out, and_71_out, and_72_out, and_73_out, and_74_out);
  or or_32 (or_32_out, and_75_out, and_76_out, and_77_out, and_78_out);
  or or_33 (or_33_out, and_79_out, and_80_out, and_81_out, and_82_out);
  not not_54 (not_54_out, S0);
  not not_55 (not_55_out, S1);
  and and_91 (and_91_out, 1'b0, not_55_out, not_54_out);
  and and_92 (and_92_out, 1'b0, not_55_out, S0);
  and and_93 (and_93_out, 1'b0, not_54_out, S1);
  and and_94 (and_94_out, 1'b1, S0, S1);
  or or_34 (or_34_out, and_91_out, and_92_out, and_93_out, and_94_out);
  xor xor_5 (xor_5_out, or_26_out, or_27_out);
  xor xor_6 (xor_6_out, or_30_out, or_31_out);
  xor xor_7 (xor_7_out, or_32_out, or_33_out);
  xor xor_8 (xor_8_out, or_28_out, or_29_out);
  xor xor_9 (xor_9_out, xor_6_out, or_38_out);
  and and_95 (and_95_out, xor_6_out, or_38_out);
  and and_96 (and_96_out, or_30_out, or_31_out);
  xor xor_10 (xor_10_out, xor_5_out, or_35_out);
  and and_97 (and_97_out, xor_5_out, or_35_out);
  and and_98 (and_98_out, or_26_out, or_27_out);
  xor xor_11 (xor_11_out, xor_7_out, or_34_out);
  and and_99 (and_99_out, xor_7_out, or_34_out);
  and and_100 (and_100_out, or_32_out, or_33_out);
  xor xor_12 (xor_12_out, xor_8_out, or_37_out);
  and and_101 (and_101_out, xor_8_out, or_37_out);
  and and_102 (and_102_out, or_28_out, or_29_out);
  or or_35 (or_35_out, and_95_out, and_96_out);
  or or_36 (or_36_out, and_97_out, and_98_out);
  or or_37 (or_37_out, and_99_out, and_100_out);
  or or_38 (or_38_out, and_101_out, and_102_out);
endmodule
